// Logisim project BabchanikViktorupdated.circ as structural Verilog: 12 circuits, main circuit CPU15
module main (
  input  Enable_Breakpoint
);

  wire chipset_1_irq, CLK, clock_1_out, cpu15_1_c, cpu15_1_e, cpu15_1_i, cpu15_1_n, cpu15_1_o, cpu15_1_z,
       KBCLR, KBIRQ, KBRD, MEMCS, nand_1_out, RE, TTYCLR, TTYWE, WE;
  wire [6:0] KBDATA, TTYDATA;
  wire [7:0] cpu15_1_srf;
  wire [14:0] ADDR, chipset_1_ivect, chipset_1_led0, chipset_1_led1, chipset_1_led2, chipset_1_led3,
       chipset_1_led4, chipset_1_led5, chipset_1_led6, chipset_1_led7, chipset_1_led8, chipset_1_led9,
       chipset_1_leda, chipset_1_ledb, chipset_1_ledc, chipset_1_ledd, chipset_1_lede, cpu15_1_ib,
       cpu15_1_pc, cpu15_1_r0, cpu15_1_r1, cpu15_1_r2, cpu15_1_r3, cpu15_1_r4, cpu15_1_r5, cpu15_1_r6,
       cpu15_1_r7, cpu15_1_srp, DATA, xnor_1_out;

  Clock clock_1 (.out(clock_1_out));
  nand nand_1 (nand_1_out, Enable_Breakpoint, xnor_1_out[0], xnor_1_out[1], xnor_1_out[2], xnor_1_out[3], xnor_1_out[4], xnor_1_out[5], xnor_1_out[6], xnor_1_out[7], xnor_1_out[8], xnor_1_out[9], xnor_1_out[10], xnor_1_out[11], xnor_1_out[12], xnor_1_out[13], xnor_1_out[14], 1'b1);
  and and_1 (CLK, clock_1_out, nand_1_out);
  assign xnor_1_out = ~(15'h36 ^ cpu15_1_pc);  // XNOR_Gate xnor_1, 15 bits wide
  LED I (.in(cpu15_1_i));
  LED Z (.in(cpu15_1_z));
  LED N (.in(cpu15_1_n));
  LED O (.in(cpu15_1_o));
  LED C (.in(cpu15_1_c));
  LED E (.in(cpu15_1_e));
  // Probe on cpu15_1_pc
  // Probe on cpu15_1_ib
  // Probe on cpu15_1_srp
  // Probe on cpu15_1_srf
  // Probe on cpu15_1_r0
  // Probe on cpu15_1_r1
  // Probe on cpu15_1_r2
  // Probe on cpu15_1_r3
  // Probe on cpu15_1_r4
  // Probe on cpu15_1_r5
  // Probe on cpu15_1_r6
  // Probe on cpu15_1_r7
  CPU15 cpu15_1 (
    .I(cpu15_1_i), .Z(cpu15_1_z), .N(cpu15_1_n), .O(cpu15_1_o), .C(cpu15_1_c), .E(cpu15_1_e),
    .PC(cpu15_1_pc), .IB(cpu15_1_ib), .SRP(cpu15_1_srp), .SRF(cpu15_1_srf), .R0(cpu15_1_r0), .R1(cpu15_1_r1),
    .R2(cpu15_1_r2), .R3(cpu15_1_r3), .R4(cpu15_1_r4), .R5(cpu15_1_r5), .R6(cpu15_1_r6), .R7(cpu15_1_r7),
    .CLK(CLK), .IRQ(chipset_1_irq), .RE(RE), .WE(WE), .ADDR(ADDR), .DATAIN(DATA), .DATAOUT(DATA));
  // Probe on ADDR
  // Probe on DATA
  // Probe on chipset_1_ivect
  RAM #(.addrWidth(15), .dataWidth(15)) ram_1 (.addr(ADDR), .data(DATA), .sel(MEMCS), .clk(CLK), .ld(RE));  // open: clr
  // Probe on TTYDATA
  CHIPSET chipset_1 (
    .RE(RE), .WE(WE), .ADDR(ADDR), .CPUDATAIN(DATA), .CPUDATAOUT(DATA), .IRQ(chipset_1_irq),
    .IVECT(chipset_1_ivect), .CLK(CLK), .MEMCS(MEMCS), .TTYWR(TTYWE), .TTYCLR(TTYCLR), .TTYDATA(TTYDATA),
    .KBRD(KBRD), .KBCLR(KBCLR), .KBIRQ(KBIRQ), .KBDATA(KBDATA), .LED0(chipset_1_led0), .LED1(chipset_1_led1),
    .LED2(chipset_1_led2), .LED3(chipset_1_led3), .LED4(chipset_1_led4), .LED5(chipset_1_led5),
    .LED6(chipset_1_led6), .LED7(chipset_1_led7), .LED8(chipset_1_led8), .LED9(chipset_1_led9),
    .LEDA(chipset_1_leda), .LEDB(chipset_1_ledb), .LEDC(chipset_1_ledc), .LEDD(chipset_1_ledd),
    .LEDE(chipset_1_lede));
  TTY tty_1 (.data(TTYDATA), .clk(CLK), .we(TTYWE), .clr(TTYCLR));
  Keyboard keyboard_1 (.clk(CLK), .re(KBRD), .clr(KBCLR), .avail(KBIRQ), .data(KBDATA));
  DotMatrix #(.matrixcols(15), .matrixrows(15)) dotmatrix_1 (
    .col0(chipset_1_led0), .col1(chipset_1_led1), .col2(chipset_1_led2), .col3(chipset_1_led3),
    .col4(chipset_1_led4), .col5(chipset_1_led5), .col6(chipset_1_led6), .col7(chipset_1_led7),
    .col8(chipset_1_led8), .col9(chipset_1_led9), .col10(chipset_1_leda), .col11(chipset_1_ledb),
    .col12(chipset_1_ledc), .col13(chipset_1_ledd), .col14(chipset_1_lede));
endmodule

// CPU
module CPU15 (
  input  [14:0] DATAIN,
  input  CLK,
  input  IRQ,
  output [14:0] PC,
  output [14:0] IB,
  output [14:0] SRP,
  output [7:0] SRF,
  output [14:0] R0,
  output [14:0] R1,
  output [14:0] R2,
  output [14:0] R3,
  output [14:0] R4,
  output [14:0] R5,
  output [14:0] R6,
  output [14:0] R7,
  output RE,
  output WE,
  output I,
  output Z,
  output [14:0] ADDR,
  output N,
  output O,
  output C,
  output E,
  output [14:0] DATAOUT
);

  wire a_register_read_enable_logic_1_out_2, ADD, ADDI, AND, and_2_out, and_3_out, and_4_out, and_5_out,
       and_6_out, and_7_out, b_register_read_enable_logic_1_out_2, BR, Cout, ena_j, INV, isFset, JMP, JSR,
       LD, LDFI, LIH, LIL0, LIL1, MOV, MOVF, MSRF, MSRP, NOP, NOT, not_2_out, Oout, OR, or_1_out, or_2_out,
       P1, P2, ROL, ROR, RTI, SHL, SHR, ST, SUB, SWI, write_to_registers_logic_1_out_3, XOR;
  wire [2:0] multiplexer_3_out;
  wire [3:2] ANDF;
  wire [7:0] new_flags;
  wire [14:0] A, A_, B, B_, bit_extender_1_out, bit_extender_2_out, bit_extender_3_out, bit_extender_4_out,
       controlled_buffer_1_out, LOAD_Res, multiplexer_1_out, multiplexer_4_out, multiplexer_6_out, New_PC,
       register_1_q, S;

  Counter #(.width(1), .max('h1)) counter_1 (.Q(P2), .clk(CLK));  // open: load, D, count, carry, clr
  not not_1 (P1, P2);
  and and_1 (ena_j, P2, or_1_out);
  and and_2 (and_2_out, P2, not_2_out);
  not not_2 (not_2_out, ena_j);
  Multiplexer #(.select(5), .width(15)) multiplexer_1 (
    .in0(LOAD_Res), .in1(S), .in2(S), .in3(S), .in4(S), .in6(S), .in9(S), .in10(LOAD_Res), .in11(LOAD_Res),
    .in12(S), .in13(S), .in14(S), .in15(S), .in17(S), .in20(S), .in21(LOAD_Res), .in24(S), .in31(S),
    .out(multiplexer_1_out), .sel(IB[14:10]));  // open: in5, in7, in8, in16, in18, in19, in22, in23, in25, in26, in27, in28, in29, in30, en
  Write_to_registers_logic write_to_registers_logic_1 (
    .opc(IB[14:10]), .in_2(P2), .out_3(write_to_registers_logic_1_out_3));
  and and_3 (and_3_out, P2, LD);
  assign controlled_buffer_1_out = and_3_out ? DATAIN : 15'bz;  // Controlled_Buffer controlled_buffer_1
  or or_1 (or_1_out, BR, JSR, JMP);
  Counter #(.width(15), .max('h7fff)) u_PC (
    .load(ena_j), .D(New_PC), .count(and_2_out), .Q(PC), .clk(CLK));  // open: carry, clr
  A_register_read_enable_logic a_register_read_enable_logic_1 (
    .out_2(a_register_read_enable_logic_1_out_2), .opc(IB[14:10]));
  Multiplexer #(.select(2), .width(15)) multiplexer_2 (
    .in0(controlled_buffer_1_out), .in1({B[14:8], 1'b1, IB[6:0]}), .in2({IB[6:0], B[7:0]}),
    .in3({B[14:8], 1'b0, IB[6:0]}), .out(LOAD_Res), .sel(IB[11:10]));  // open: en
  B_register_read_enable_logic b_register_read_enable_logic_1 (
    .out_2(b_register_read_enable_logic_1_out_2), .opc(IB[14:10]));
  Register #(.width(15)) u_IB (.D(DATAIN), .en(P1), .Q(IB), .clk(CLK));  // open: clr
  Register_File register_file_1 (
    .W_data(multiplexer_1_out), .W_en(write_to_registers_logic_1_out_3), .W_addr(IB[9:7]),
    .AR_en(a_register_read_enable_logic_1_out_2), .AR_addr(IB[6:4]),
    .BR_en(b_register_read_enable_logic_1_out_2), .BR_addr(multiplexer_3_out), .r0(R0), .r1(R1), .out_12(R2),
    .out_13(R3), .out_14(R4), .out_15(R5), .out_16(R6), .r7(R7), .A(A), .B(B));
  Multiplexer #(.select(5), .width(3)) multiplexer_3 (
    .in0(IB[9:7]), .in1(IB[3:1]), .in2(IB[3:1]), .in3(IB[6:4]), .in4(IB[3:1]), .in9(IB[3:1]), .in10(IB[9:7]),
    .in11(IB[9:7]), .in16(IB[9:7]), .in17(IB[3:1]), .in18(IB[9:7]), .in21(IB[9:7]), .in31(IB[3:1]),
    .out(multiplexer_3_out), .sel(IB[14:10]));  // open: in5, in6, in7, in8, in12, in13, in14, in15, in19, in20, in22, in23, in24, in25, in26, in27, in28, in29, in30, en
  Multiplexer #(.select(5), .width(15)) multiplexer_4 (
    .in0(S), .in16(S), .out(multiplexer_4_out), .sel(IB[14:10]));  // open: in1, in2, in3, in4, in5, in6, in7, in8, in9, in10, in11, in12, in13, in14, in15, in17, in18, in19, in20, in21, in22, in23, in24, in25, in26, in27, in28, in29, in30, in31, en
  or or_2 (or_2_out, INV, NOT, SUB, XOR, XOR, ADDI, ADD, AND, OR);
  Multiplexer #(.width(15)) multiplexer_5 (.in0(PC), .in1(multiplexer_4_out), .out(ADDR), .sel(P2));  // open: en
  and and_4 (and_4_out, P2, or_2_out);
  assign bit_extender_1_out = {{14{1'b0}}, 1'b1};  // Bit_Extender bit_extender_1
  assign bit_extender_2_out = {{8{IB[6]}}, IB[6:0]};  // Bit_Extender bit_extender_2
  Register #(.width(15)) register_1 (.D(B), .Q(register_1_q), .clk(CLK));  // open: en, clr
  Flags_register flags_register_1 (
    .W_en(and_4_out), .R_(IB[9:7]), .I_flag(I), .out_7(Z), .out_8(N), .out_9(O), .out_10(C), .out_11(E),
    .A(1'b1), .\input (new_flags), .flag_br(isFset));  // open: extra_flag
  ALU alu_1 (.CinF(C), .A(A_), .B(B_), .opcode(IB[14:10]), .CoutF(Cout), .N(ANDF[3]), .O(Oout), .Z(ANDF[2]), .S(S));
  Multiplexer #(.width(15)) multiplexer_6 (
    .in0(bit_extender_1_out), .in1(bit_extender_2_out), .out(multiplexer_6_out), .sel(isFset));  // open: en
  assign bit_extender_3_out = {{14{1'b0}}, 1'b1};  // Bit_Extender bit_extender_3
  and and_5 (and_5_out, P2, ST);
  assign DATAOUT = and_5_out ? register_1_q : 15'bz;  // Controlled_Buffer controlled_buffer_2
  Multiplexer #(.select(5), .width(15)) multiplexer_7 (
    .in0(A), .in1(A), .in2(A), .in3(A), .in4(A), .in6(A), .in8(multiplexer_6_out), .in9(A), .in12(A),
    .in13(A), .in14(A), .in15(A), .in16(A), .in17(A), .in20(A), .in24(bit_extender_3_out), .in31(A),
    .out(A_), .sel(IB[14:10]));  // open: in5, in7, in10, in11, in18, in19, in21, in22, in23, in25, in26, in27, in28, in29, in30, en
  Multiplexer #(.select(5), .width(8)) multiplexer_8 (
    .in1({1'b0, E, Cout, Oout, ANDF, I, 1'b1}), .in2({1'b0, E, C, O, ANDF, I, 1'b1}),
    .in3({1'b0, E, C, O, ANDF, I, 1'b1}), .in4({1'b0, E, Cout, Oout, ANDF, I, 1'b1}),
    .in6({1'b0, E, C, O, ANDF, I, 1'b1}), .in9({1'b0, E, C, O, ANDF, I, 1'b1}),
    .in12({1'b0, E, Cout, O, ANDF, I, 1'b1}), .in13({1'b0, E, Cout, O, ANDF, I, 1'b1}),
    .in14({1'b0, E, Cout, O, ANDF, I, 1'b1}), .in15({1'b0, E, Cout, O, ANDF, I, 1'b1}),
    .in17({1'b0, E, C, O, ANDF, I, 1'b1}), .in20({1'b0, E, Cout, Oout, ANDF, I, 1'b1}), .out(new_flags),
    .sel(IB[14:10]));  // open: in0, in5, in7, in8, in10, in11, in16, in18, in19, in21, in22, in23, in24, in25, in26, in27, in28, in29, in30, in31, en
  assign bit_extender_4_out = {{11{IB[3]}}, IB[3:0]};  // Bit_Extender bit_extender_4
  Multiplexer #(.select(5), .width(15)) multiplexer_9 (
    .in0(bit_extender_4_out), .in1(B), .in2(B), .in3(B), .in4(B), .in8(PC), .in9(B),
    .in16(bit_extender_4_out), .in17(B), .in20(bit_extender_4_out), .in24(PC), .out(B_), .sel(IB[14:10]));  // open: in5, in6, in7, in10, in11, in12, in13, in14, in15, in18, in19, in21, in22, in23, in25, in26, in27, in28, in29, in30, in31, en
  and and_6 (and_6_out, P2, LD);
  or or_3 (RE, P1, and_6_out);
  Demultiplexer #(.select(5), .enable("false")) demultiplexer_1 (
    .out0(LD), .out1(SUB), .out2(AND), .out3(INV), .out4(ADD), .out6(NOT), .out7(NOP), .out8(BR), .out9(OR),
    .out10(LIH), .out11(LIL0), .out12(ROR), .out13(ROL), .out14(SHR), .out15(SHL), .out16(ST), .out17(XOR),
    .out18(JMP), .out19(LDFI), .out20(ADDI), .out21(LIL1), .out24(JSR), .out25(MOVF), .out26(MSRP),
    .out27(MSRF), .out28(SWI), .out29(RTI), .out31(MOV), .in(1'b1), .sel(IB[14:10]));  // open: out5, out22, out23, out30
  Multiplexer #(.select(5), .width(15)) multiplexer_10 (
    .in8(S), .in18(B), .in24(A), .out(New_PC), .sel(IB[14:10]));  // open: in0, in1, in2, in3, in4, in5, in6, in7, in9, in10, in11, in12, in13, in14, in15, in16, in17, in19, in20, in21, in22, in23, in25, in26, in27, in28, in29, in30, in31, en
  and and_7 (and_7_out, P2, ST);
  buf or_4 (WE, and_7_out);  // OR_Gate

  // Other names for the same wires on the sheet: ANDF (some bits) = {E, C, O, I}; RL[7:0] = B[7:0]; RH[6:0] = B[14:8];
  //   DATA[14:0] = DATAIN; VAL[6:0] = IB[6:0]; VAL_2[2:0] = IB[6:4]; R_[2:0] = IB[9:7]; OPC[4:0] = IB[14:10];
  //   OFFSET[3:0] = IB[3:0]; VAL_0 = IB[0]; VAL_1[2:0] = IB[3:1]; RSLFF[6:1] = {E, Cout, O, ANDF, I}; Zout = ANDF[2];
  //   Nout = ANDF[3]

  // Notes on the sheet:
  //   When to enable reading
endmodule

module CHIPSET (
  input  RE,
  input  WE,
  input  [14:0] ADDR,
  input  [14:0] CPUDATAIN,
  input  KBIRQ,
  input  [6:0] KBDATA,
  input  CLK,
  output MEMCS,
  output TTYWR,
  output [14:0] IVECT,
  output TTYCLR,
  output [6:0] TTYDATA,
  output KBRD,
  output KBCLR,
  output [14:0] CPUDATAOUT,
  output IRQ,
  output [14:0] LED0,
  output [14:0] LED1,
  output [14:0] LED2,
  output [14:0] LED3,
  output [14:0] LED4,
  output [14:0] LED5,
  output [14:0] LED6,
  output [14:0] LED7,
  output [14:0] LED8,
  output [14:0] LED9,
  output [14:0] LEDA,
  output [14:0] LEDB,
  output [14:0] LEDC,
  output [14:0] LEDD,
  output [14:0] LEDE
);

  wire and_1_out, and_8_out, and_10_out, DATA7, IOCS, IVECTADDR, IVECTEN, IVECTRE, KBCS, LED0EN, LED0END,
       LED1EN, LED1END, LED2EN, LED2END, LED3EN, LED3END, LED4EN, LED4END, LED5EN, LED5END, LED6EN, LED6END,
       LED7EN, LED7END, LED8EN, LED8END, LED9EN, LED9END, LEDAEN, LEDAEND, LEDBEN, LEDBEND, LEDCEN, LEDCEND,
       LEDCS, LEDDEN, LEDDEND, LEDEEN, LEDEEND, LEDFEND, LEDRE, multiplexer_17_out, multiplexer_18_out, RWE,
       TTYCS;
  wire [14:0] DATAL0, DATAL1, DATAL2, DATAL3, DATAL4, DATAL5, DATAL6, DATAL7, DATAL8, DATAL9, DATALA, DATALB,
       DATALC, DATALD, DATALE, LEDDATA;
  wire [14:8] KBDATA15;

  assign CPUDATAOUT = KBRD ? {KBDATA15, DATA7, KBDATA} : 15'bz;  // Controlled_Buffer controlled_buffer_1
  assign CPUDATAOUT = LEDRE ? LEDDATA : 15'bz;  // Controlled_Buffer controlled_buffer_2
  assign CPUDATAOUT = IVECTRE ? IVECT : 15'bz;  // Controlled_Buffer controlled_buffer_3
  Register #(.width(15)) register_1 (.D(DATAL0), .en(LED0EN), .Q(LED0), .clk(CLK));  // open: clr
  Register #(.width(15)) register_2 (.D(DATAL1), .en(LED1EN), .Q(LED1), .clk(CLK));  // open: clr
  Register #(.width(15)) register_3 (.D(DATAL2), .en(LED2EN), .Q(LED2), .clk(CLK));  // open: clr
  Register #(.width(15)) register_4 (.D(DATAL3), .en(LED3EN), .Q(LED3), .clk(CLK));  // open: clr
  Register #(.width(15)) register_5 (.D(DATAL4), .en(LED4EN), .Q(LED4), .clk(CLK));  // open: clr
  and and_1 (and_1_out, WE, LEDCS);
  Decoder #(.select(4), .disabled(0)) decoder_1 (
    .out0(LED0END), .out1(LED1END), .out2(LED2END), .out3(LED3END), .out4(LED4END), .out5(LED5END),
    .out6(LED6END), .out7(LED7END), .out8(LED8END), .out9(LED9END), .out10(LEDAEND), .out11(LEDBEND),
    .out12(LEDCEND), .out13(LEDDEND), .out14(LEDEEND), .out15(LEDFEND), .sel(ADDR[3:0]), .en(and_1_out));
  Register #(.width(15)) register_6 (.D(DATAL5), .en(LED5EN), .Q(LED5), .clk(CLK));  // open: clr
  Register #(.width(15)) register_7 (.D(DATAL6), .en(LED6EN), .Q(LED6), .clk(CLK));  // open: clr
  Register #(.width(15)) register_8 (.D(DATAL7), .en(LED7EN), .Q(LED7), .clk(CLK));  // open: clr
  Register #(.width(15)) register_9 (.D(DATAL8), .en(LED8EN), .Q(LED8), .clk(CLK));  // open: clr
  Register #(.width(15)) register_10 (.D(DATAL9), .en(LED9EN), .Q(LED9), .clk(CLK));  // open: clr
  or or_1 (LED0EN, LED0END, LEDFEND);
  or or_2 (LED1EN, LED1END, LEDFEND);
  or or_3 (LED2EN, LED2END, LEDFEND);
  or or_4 (LED3EN, LED3END, LEDFEND);
  or or_5 (LED4EN, LED4END, LEDFEND);
  or or_6 (LED5EN, LED5END, LEDFEND);
  or or_7 (LED6EN, LED6END, LEDFEND);
  or or_8 (LED7EN, LED7END, LEDFEND);
  or or_9 (LED8EN, LED8END, LEDFEND);
  or or_10 (LED9EN, LED9END, LEDFEND);
  or or_11 (LEDAEN, LEDAEND, LEDFEND);
  or or_12 (LEDBEN, LEDBEND, LEDFEND);
  or or_13 (LEDCEN, LEDCEND, LEDFEND);
  or or_14 (LEDDEN, LEDDEND, LEDFEND);
  or or_15 (LEDEEN, LEDEEND, LEDFEND);
  Pull_Resistor pull_resistor_1 (.node(KBDATA15[14]));
  Pull_Resistor pull_resistor_2 (.node(KBDATA15[13]));
  Pull_Resistor pull_resistor_3 (.node(KBDATA15[11]));
  Pull_Resistor pull_resistor_4 (.node(KBDATA15[12]));
  Pull_Resistor pull_resistor_5 (.node(KBDATA15[10]));
  Pull_Resistor pull_resistor_6 (.node(DATA7));
  Pull_Resistor pull_resistor_7 (.node(KBDATA15[8]));
  Pull_Resistor pull_resistor_8 (.node(KBDATA15[9]));
  Register #(.width(15)) register_11 (.D(DATALA), .en(LEDAEN), .Q(LEDA), .clk(CLK));  // open: clr
  Register #(.width(15)) register_12 (.D(DATALB), .en(LEDBEN), .Q(LEDB), .clk(CLK));  // open: clr
  Register #(.width(15)) register_13 (.D(DATALC), .en(LEDCEN), .Q(LEDC), .clk(CLK));  // open: clr
  Register #(.width(15)) register_14 (.D(DATALD), .en(LEDDEN), .Q(LEDD), .clk(CLK));  // open: clr
  Register #(.width(15)) register_15 (.D(DATALE), .en(LEDEEN), .Q(LEDE), .clk(CLK));  // open: clr
  Multiplexer #(.width(15), .enable("false")) multiplexer_1 (.in0(CPUDATAIN), .in1(LED1), .out(DATAL0), .sel(LEDFEND));
  Multiplexer #(.width(15), .enable("false")) multiplexer_2 (.in0(CPUDATAIN), .in1(LED2), .out(DATAL1), .sel(LEDFEND));
  Multiplexer #(.width(15), .enable("false")) multiplexer_3 (.in0(CPUDATAIN), .in1(LED3), .out(DATAL2), .sel(LEDFEND));
  Multiplexer #(.width(15), .enable("false")) multiplexer_4 (.in0(CPUDATAIN), .in1(LED4), .out(DATAL3), .sel(LEDFEND));
  Multiplexer #(.width(15), .enable("false")) multiplexer_5 (.in0(CPUDATAIN), .in1(LED5), .out(DATAL4), .sel(LEDFEND));
  Multiplexer #(.select(4), .width(15)) multiplexer_6 (
    .in0(LED0), .in1(LED1), .in2(LED2), .in3(LED3), .in4(LED4), .in5(LED5), .in6(LED6), .in7(LED7),
    .in8(LED8), .in9(LED9), .in10(LEDA), .in11(LEDB), .in12(LEDC), .in13(LEDD), .in14(LEDE),
    .in15({15{1'b0}}), .out(LEDDATA), .sel(ADDR[3:0]), .en(LEDRE));
  Multiplexer #(.width(15), .enable("false")) multiplexer_7 (.in0(CPUDATAIN), .in1(LED6), .out(DATAL5), .sel(LEDFEND));
  Multiplexer #(.width(15), .enable("false")) multiplexer_8 (.in0(CPUDATAIN), .in1(LED7), .out(DATAL6), .sel(LEDFEND));
  Multiplexer #(.width(15), .enable("false")) multiplexer_9 (.in0(CPUDATAIN), .in1(LED8), .out(DATAL7), .sel(LEDFEND));
  Multiplexer #(.width(15), .enable("false")) multiplexer_10 (.in0(CPUDATAIN), .in1(LED9), .out(DATAL8), .sel(LEDFEND));
  Multiplexer #(.width(15), .enable("false")) multiplexer_11 (.in0(CPUDATAIN), .in1(LEDA), .out(DATAL9), .sel(LEDFEND));
  and and_2 (LEDRE, RE, LEDCS);
  Multiplexer #(.width(15), .enable("false")) multiplexer_12 (.in0(CPUDATAIN), .in1(LEDB), .out(DATALA), .sel(LEDFEND));
  Multiplexer #(.width(15), .enable("false")) multiplexer_13 (.in0(CPUDATAIN), .in1(LEDC), .out(DATALB), .sel(LEDFEND));
  Multiplexer #(.width(15), .enable("false")) multiplexer_14 (.in0(CPUDATAIN), .in1(LEDD), .out(DATALC), .sel(LEDFEND));
  Multiplexer #(.width(15), .enable("false")) multiplexer_15 (.in0(CPUDATAIN), .in1(LEDE), .out(DATALD), .sel(LEDFEND));
  Multiplexer #(.width(15), .enable("false")) multiplexer_16 (
    .in0(CPUDATAIN), .in1(CPUDATAIN), .out(DATALE), .sel(LEDFEND));
  and and_3 (IOCS, ADDR[5], ADDR[6], ADDR[7], ADDR[8], ADDR[9], ADDR[10], ADDR[11], ADDR[12], ADDR[13], ADDR[14], 1'b1);
  and and_4 (TTYCS, IOCS, ADDR[0], ~ADDR[1], ~ADDR[2], ~ADDR[3], ADDR[4]);  // AND_Gate
  and and_5 (KBCS, IOCS, ~ADDR[0], ~ADDR[1], ~ADDR[2], ~ADDR[3], ADDR[4]);  // AND_Gate
  and and_6 (IVECTADDR, ADDR[0], ADDR[1], ADDR[2], ADDR[3], ADDR[4], ADDR[5], ADDR[6], ADDR[7], ADDR[8], ADDR[9], ADDR[10], ADDR[11], ADDR[12], ADDR[13], ADDR[14]);
  and and_7 (TTYWR, TTYCS, WE);
  and and_8 (and_8_out, TTYWR, DATA7);
  and and_9 (KBRD, KBCS, RE);
  and and_10 (and_10_out, KBCS, WE);
  Multiplexer #(.enable("false")) multiplexer_17 (.in0(and_10_out), .in1(1'b0), .out(multiplexer_17_out), .sel(KBCLR));
  and and_11 (LEDCS, IOCS, ~ADDR[4], RWE);  // AND_Gate
  and and_12 (IVECTEN, IVECTADDR, WE);
  and and_13 (IVECTRE, IVECTADDR, RE);
  or or_16 (RWE, RE, WE);
  and and_14 (MEMCS, ~IOCS, RWE);  // AND_Gate
  Multiplexer #(.enable("false")) multiplexer_18 (.in0(and_8_out), .in1(1'b0), .out(multiplexer_18_out), .sel(TTYCLR));
  D_Flip_Flop d_ff_1 (.clk(CLK), .D(multiplexer_17_out), .Q(KBCLR));  // open: Qn, preset, en, reset
  Register #(.width(15)) register_16 (.D(CPUDATAIN), .en(IVECTEN), .Q(IVECT), .clk(CLK));  // open: clr
  D_Flip_Flop d_ff_2 (.clk(CLK), .D(multiplexer_18_out), .Q(TTYCLR));  // open: Qn, preset, en, reset

  assign IRQ = KBIRQ;
  assign TTYDATA = CPUDATAIN[6:0];

  // Other names for the same wires on the sheet: DATA[14:0] = CPUDATAIN; KBDATA15[7:0] = {DATA7, KBDATA}
endmodule

module _1_bit_Adder (
  input  A,
  input  B,
  input  Cin,
  output S,
  output Cout
);

  wire and_1_out, and_2_out, and_3_out;

  xor xor_1 (S, A, B, Cin);
  and and_1 (and_1_out, A, B);
  and and_2 (and_2_out, A, Cin);
  and and_3 (and_3_out, B, Cin);
  or or_1 (Cout, and_1_out, and_2_out, and_3_out);
endmodule

module _15_bit_Adder (
  input  [14:0] A,
  input  [14:0] B,
  input  Control,
  output Cout,
  output [14:0] S
);

  wire n1_bit_adder_1_cout, n1_bit_adder_2_cout, n1_bit_adder_3_cout, n1_bit_adder_4_cout,
       n1_bit_adder_5_cout, n1_bit_adder_6_cout, n1_bit_adder_7_cout, n1_bit_adder_8_cout,
       n1_bit_adder_9_cout, n1_bit_adder_10_cout, n1_bit_adder_11_cout, n1_bit_adder_12_cout,
       n1_bit_adder_13_cout, n1_bit_adder_14_cout, xor_1_out, xor_2_out, xor_3_out, xor_4_out, xor_5_out,
       xor_6_out, xor_7_out, xor_8_out, xor_9_out, xor_10_out, xor_11_out, xor_12_out, xor_13_out,
       xor_14_out, xor_15_out;

  xor xor_1 (xor_1_out, Control, B[0]);
  _1_bit_Adder u_1_bit_adder_1 (.A(A[0]), .B(xor_1_out), .Cin(Control), .S(S[0]), .Cout(n1_bit_adder_1_cout));
  xor xor_2 (xor_2_out, Control, B[1]);
  xor xor_3 (xor_3_out, Control, B[2]);
  _1_bit_Adder u_1_bit_adder_2 (
    .A(A[1]), .B(xor_2_out), .Cin(n1_bit_adder_1_cout), .S(S[1]), .Cout(n1_bit_adder_2_cout));
  _1_bit_Adder u_1_bit_adder_3 (
    .A(A[2]), .B(xor_3_out), .Cin(n1_bit_adder_2_cout), .S(S[2]), .Cout(n1_bit_adder_3_cout));
  xor xor_4 (xor_4_out, Control, B[4]);
  xor xor_5 (xor_5_out, Control, B[3]);
  _1_bit_Adder u_1_bit_adder_4 (
    .A(A[3]), .B(xor_5_out), .Cin(n1_bit_adder_3_cout), .S(S[3]), .Cout(n1_bit_adder_4_cout));
  xor xor_6 (xor_6_out, Control, B[5]);
  _1_bit_Adder u_1_bit_adder_5 (
    .A(A[5]), .B(xor_6_out), .Cin(n1_bit_adder_6_cout), .S(S[5]), .Cout(n1_bit_adder_5_cout));
  _1_bit_Adder u_1_bit_adder_6 (
    .A(A[4]), .B(xor_4_out), .Cin(n1_bit_adder_4_cout), .S(S[4]), .Cout(n1_bit_adder_6_cout));
  xor xor_7 (xor_7_out, Control, B[7]);
  xor xor_8 (xor_8_out, Control, B[6]);
  _1_bit_Adder u_1_bit_adder_7 (
    .A(A[7]), .B(xor_7_out), .Cin(n1_bit_adder_8_cout), .S(S[7]), .Cout(n1_bit_adder_7_cout));
  _1_bit_Adder u_1_bit_adder_8 (
    .A(A[6]), .B(xor_8_out), .Cin(n1_bit_adder_5_cout), .S(S[6]), .Cout(n1_bit_adder_8_cout));
  xor xor_9 (xor_9_out, Control, B[8]);
  _1_bit_Adder u_1_bit_adder_9 (
    .A(A[8]), .B(xor_9_out), .Cin(n1_bit_adder_7_cout), .S(S[8]), .Cout(n1_bit_adder_9_cout));
  xor xor_10 (xor_10_out, Control, B[9]);
  xor xor_11 (xor_11_out, Control, B[10]);
  _1_bit_Adder u_1_bit_adder_10 (
    .A(A[10]), .B(xor_11_out), .Cin(n1_bit_adder_11_cout), .S(S[10]), .Cout(n1_bit_adder_10_cout));
  _1_bit_Adder u_1_bit_adder_11 (
    .A(A[9]), .B(xor_10_out), .Cin(n1_bit_adder_9_cout), .S(S[9]), .Cout(n1_bit_adder_11_cout));
  xor xor_12 (xor_12_out, Control, B[11]);
  xor xor_13 (xor_13_out, Control, B[12]);
  _1_bit_Adder u_1_bit_adder_12 (
    .A(A[11]), .B(xor_12_out), .Cin(n1_bit_adder_10_cout), .S(S[11]), .Cout(n1_bit_adder_12_cout));
  xor xor_14 (xor_14_out, Control, B[13]);
  _1_bit_Adder u_1_bit_adder_13 (
    .A(A[13]), .B(xor_14_out), .Cin(n1_bit_adder_14_cout), .S(S[13]), .Cout(n1_bit_adder_13_cout));
  _1_bit_Adder u_1_bit_adder_14 (
    .A(A[12]), .B(xor_13_out), .Cin(n1_bit_adder_12_cout), .S(S[12]), .Cout(n1_bit_adder_14_cout));
  xor xor_15 (xor_15_out, Control, B[14]);
  _1_bit_Adder u_1_bit_adder_15 (.A(A[14]), .B(xor_15_out), .Cin(n1_bit_adder_13_cout), .S(S[14]), .Cout(Cout));
endmodule

module ALU (
  input  CinF,
  input  [14:0] A,
  input  [14:0] B,
  input  [4:0] opcode,
  output CoutF,
  output N,
  output O,
  output Z,
  output [14:0] S
);

  wire and_1_out, and_2_out, CoutF_ADD, CoutF_LRSR, or_1_out;
  wire [14:0] ADD, AND, LRSR, multiplexer_1_out, NOT, OR, XOR;

  RL_Shifter_Rotator rl_shifter_rotator_1 (.CinF(CinF), .A(A), .in_3(opcode[1:0]), .CoutF(CoutF_LRSR), .S(LRSR));
  Multiplexer #(.width(15)) multiplexer_1 (
    .in0(A), .in1({15{1'b0}}), .out(multiplexer_1_out), .sel(opcode[1]));  // open: en
  and and_1 (and_1_out, B[14], ~N, A[14]);  // AND_Gate
  or or_1 (or_1_out, and_1_out, and_2_out);
  and and_2 (and_2_out, ~B[14], N, ~A[14]);  // AND_Gate
  assign NOT = ~A;  // NOT_Gate not_1, 15 bits wide
  assign XOR = A ^ B;  // XOR_Gate xor_1, 15 bits wide
  assign OR = A | B;  // OR_Gate or_2, 15 bits wide
  assign AND = A & B;  // AND_Gate and_3, 15 bits wide
  _15_bit_Adder u_15_bit_adder_1 (.A(multiplexer_1_out), .Control(opcode[0]), .S(ADD), .Cout(CoutF_ADD), .B(B));
  and and_4 (O, or_1_out, ~opcode[0]);  // AND_Gate
  nor nor_1 (Z, N, S[13], S[12], S[11], S[10], S[9], S[8], S[7], S[6], S[5], S[4], S[3], S[2], S[1], S[0]);
  Multiplexer #(.select(5), .width(15)) multiplexer_2 (
    .in0(ADD), .in1(ADD), .in2(AND), .in3(ADD), .in4(ADD), .in6(NOT), .in7(A), .in8(ADD), .in9(OR),
    .in12(LRSR), .in13(LRSR), .in14(LRSR), .in15(LRSR), .in16(ADD), .in17(XOR), .in20(ADD), .in24(ADD),
    .in31(A), .out({N, S[13:0]}), .sel(opcode));  // open: in5, in10, in11, in18, in19, in21, in22, in23, in25, in26, in27, in28, in29, in30, en
  Multiplexer multiplexer_3 (.in0(CoutF_ADD), .in1(CoutF_LRSR), .out(CoutF), .sel(opcode[3]));  // open: en

  assign S[14] = N;

  // Other names for the same wires on the sheet: NOOP[14:0] = A; S0 = opcode[0]; S1 = opcode[1]; S3 = opcode[3];
  //   sign_S = N

  // Notes on the sheet:
  //   Selects proper carry bit based on opcode
endmodule

module RL_Shifter_Rotator (
  input  CinF,
  input  [14:0] A,
  input  [1:0] in_3,
  output CoutF,
  output [14:0] S
);

  Multiplexer #(.select(2)) multiplexer_1 (
    .in0(CinF), .in1(A[13]), .in2(A[14]), .in3(A[13]), .out(S[14]), .sel(in_3));  // open: en
  Multiplexer #(.select(2)) multiplexer_2 (
    .in0(A[14]), .in1(A[12]), .in2(A[14]), .in3(A[12]), .out(S[13]), .sel(in_3));  // open: en
  Multiplexer #(.select(2)) multiplexer_3 (
    .in0(A[13]), .in1(A[11]), .in2(A[13]), .in3(A[11]), .out(S[12]), .sel(in_3));  // open: en
  Multiplexer #(.select(2)) multiplexer_4 (
    .in0(A[12]), .in1(A[10]), .in2(A[12]), .in3(A[10]), .out(S[11]), .sel(in_3));  // open: en
  Multiplexer #(.select(2)) multiplexer_5 (
    .in0(A[11]), .in1(A[9]), .in2(A[11]), .in3(A[9]), .out(S[10]), .sel(in_3));  // open: en
  Multiplexer #(.select(2)) multiplexer_6 (
    .in0(A[10]), .in1(A[8]), .in2(A[10]), .in3(A[8]), .out(S[9]), .sel(in_3));  // open: en
  Multiplexer #(.select(2)) multiplexer_7 (
    .in0(A[9]), .in1(A[7]), .in2(A[9]), .in3(A[7]), .out(S[8]), .sel(in_3));  // open: en
  Multiplexer #(.select(2)) multiplexer_8 (
    .in0(A[8]), .in1(A[6]), .in2(A[8]), .in3(A[6]), .out(S[7]), .sel(in_3));  // open: en
  Multiplexer #(.select(2)) multiplexer_9 (
    .in0(A[7]), .in1(A[5]), .in2(A[7]), .in3(A[5]), .out(S[6]), .sel(in_3));  // open: en
  Multiplexer #(.select(2)) multiplexer_10 (
    .in0(A[6]), .in1(A[4]), .in2(A[6]), .in3(A[4]), .out(S[5]), .sel(in_3));  // open: en
  Multiplexer #(.select(2)) multiplexer_11 (
    .in0(A[5]), .in1(A[3]), .in2(A[5]), .in3(A[3]), .out(S[4]), .sel(in_3));  // open: en
  Multiplexer #(.select(2)) multiplexer_12 (
    .in0(A[4]), .in1(A[2]), .in2(A[4]), .in3(A[2]), .out(S[3]), .sel(in_3));  // open: en
  Multiplexer #(.select(2)) multiplexer_13 (
    .in0(A[3]), .in1(A[1]), .in2(A[3]), .in3(A[1]), .out(S[2]), .sel(in_3));  // open: en
  Multiplexer #(.select(2)) multiplexer_14 (
    .in0(A[2]), .in1(A[0]), .in2(A[2]), .in3(A[0]), .out(S[1]), .sel(in_3));  // open: en
  Multiplexer #(.select(2)) multiplexer_15 (
    .in0(A[1]), .in1(CinF), .in2(A[1]), .in3(1'b0), .out(S[0]), .sel(in_3));  // open: en
  Multiplexer #(.select(2)) multiplexer_16 (
    .in0(A[0]), .in1(A[14]), .in2(A[0]), .in3(A[14]), .out(CoutF), .sel(in_3));  // open: en
endmodule

// Register \nFile
module Register_File (
  input  [14:0] W_data,
  input  W_en,
  input  [2:0] W_addr,
  input  AR_en,
  input  [2:0] AR_addr,
  input  BR_en,
  input  [2:0] BR_addr,
  output [14:0] A,
  output [14:0] B,
  output [14:0] r0,
  output [14:0] r1,
  output [14:0] out_12,
  output [14:0] out_13,
  output [14:0] out_14,
  output [14:0] out_15,
  output [14:0] out_16,
  output [14:0] r7
);

  wire A_r0, A_r1, A_r2, A_r3, A_r4, A_r5, A_r6, A_r7, B_r0, B_r1, B_r2, B_r3, B_r4, B_r5, B_r6, B_r7,
       clk_out, decoder_1_out0, decoder_1_out1, decoder_1_out2, decoder_1_out3, decoder_1_out4,
       decoder_1_out5, decoder_1_out6, decoder_1_out7;

  Decoder #(.select(3), .disabled(0)) decoder_1 (
    .out0(decoder_1_out0), .out1(decoder_1_out1), .out2(decoder_1_out2), .out3(decoder_1_out3),
    .out4(decoder_1_out4), .out5(decoder_1_out5), .out6(decoder_1_out6), .out7(decoder_1_out7), .sel(W_addr),
    .en(W_en));
  Decoder #(.select(3), .disabled(0)) decoder_2 (
    .out0(A_r0), .out1(A_r1), .out2(A_r2), .out3(A_r3), .out4(A_r4), .out5(A_r5), .out6(A_r6), .out7(A_r7),
    .sel(AR_addr), .en(AR_en));
  Decoder #(.select(3), .disabled(0)) decoder_3 (
    .out0(B_r0), .out1(B_r1), .out2(B_r2), .out3(B_r3), .out4(B_r4), .out5(B_r5), .out6(B_r6), .out7(B_r7),
    .sel(BR_addr), .en(BR_en));
  Register #(.width(15)) register_1 (.D(W_data), .en(decoder_1_out0), .Q(r0), .clk(clk_out));  // open: clr
  Register #(.width(15)) register_2 (.D(W_data), .en(decoder_1_out1), .Q(r1), .clk(clk_out));  // open: clr
  Register #(.width(15)) register_3 (.D(W_data), .en(decoder_1_out2), .Q(out_12), .clk(clk_out));  // open: clr
  Register #(.width(15)) register_4 (.D(W_data), .en(decoder_1_out3), .Q(out_13), .clk(clk_out));  // open: clr
  Register #(.width(15)) register_5 (.D(W_data), .en(decoder_1_out4), .Q(out_14), .clk(clk_out));  // open: clr
  Register #(.width(15)) register_6 (.D(W_data), .en(decoder_1_out5), .Q(out_15), .clk(clk_out));  // open: clr
  Register #(.width(15)) register_7 (.D(W_data), .en(decoder_1_out6), .Q(out_16), .clk(clk_out));  // open: clr
  Register #(.width(15)) register_8 (.D(W_data), .en(decoder_1_out7), .Q(r7), .clk(clk_out));  // open: clr
  Clock clk (.out(clk_out));
  assign A = A_r0 ? r0 : 15'bz;  // Controlled_Buffer controlled_buffer_1
  assign B = B_r0 ? r0 : 15'bz;  // Controlled_Buffer controlled_buffer_2
  assign A = A_r1 ? r1 : 15'bz;  // Controlled_Buffer controlled_buffer_3
  assign B = B_r1 ? r1 : 15'bz;  // Controlled_Buffer controlled_buffer_4
  assign A = A_r2 ? out_12 : 15'bz;  // Controlled_Buffer controlled_buffer_5
  assign B = B_r2 ? out_12 : 15'bz;  // Controlled_Buffer controlled_buffer_6
  assign A = A_r3 ? out_13 : 15'bz;  // Controlled_Buffer controlled_buffer_7
  assign B = B_r3 ? out_13 : 15'bz;  // Controlled_Buffer controlled_buffer_8
  assign A = A_r4 ? out_14 : 15'bz;  // Controlled_Buffer controlled_buffer_9
  assign B = B_r4 ? out_14 : 15'bz;  // Controlled_Buffer controlled_buffer_10
  assign A = A_r5 ? out_15 : 15'bz;  // Controlled_Buffer controlled_buffer_11
  assign B = B_r5 ? out_15 : 15'bz;  // Controlled_Buffer controlled_buffer_12
  assign A = A_r6 ? out_16 : 15'bz;  // Controlled_Buffer controlled_buffer_13
  assign B = B_r6 ? out_16 : 15'bz;  // Controlled_Buffer controlled_buffer_14
  assign A = A_r7 ? r7 : 15'bz;  // Controlled_Buffer controlled_buffer_15
  assign B = B_r7 ? r7 : 15'bz;  // Controlled_Buffer controlled_buffer_16

  // Other names for the same wires on the sheet: R2[14:0] = out_12; R3[14:0] = out_13; R4[14:0] = out_14;
  //   R5[14:0] = out_15; R6[14:0] = out_16
endmodule

module Write_to_registers_logic (
  input  [4:0] opc,
  input  in_2,
  output out_3
);

  wire ADD, ADDI, AND, and_1_out, BR, INV, JMP, JSR, LD, LDFI, LIH, LIL0, LIL1, MOV, MOVF, MSRF, MSRP, NOP,
       NOT, OR, or_1_out, ROL, ROR, RTI, SHL, SHR, ST, SUB, SWI, XOR;

  and and_1 (and_1_out, ADDI, in_2);
  or or_1 (or_1_out, INV, MOV, SUB, and_1_out, ADD, AND, LD, NOT, XOR, OR, JSR, LIH, LIL0, LIL1);
  or or_2 (out_3, ROR, ROL, or_1_out, SHL, SHR);
  Demultiplexer #(.select(5), .enable("false")) demultiplexer_1 (
    .out0(LD), .out1(SUB), .out2(AND), .out3(INV), .out4(ADD), .out6(NOT), .out7(NOP), .out8(BR), .out9(OR),
    .out10(LIH), .out11(LIL0), .out12(ROR), .out13(ROL), .out14(SHR), .out15(SHL), .out16(ST), .out17(XOR),
    .out18(JMP), .out19(LDFI), .out20(ADDI), .out21(LIL1), .out24(JSR), .out25(MOVF), .out26(MSRP),
    .out27(MSRF), .out28(SWI), .out29(RTI), .out31(MOV), .in(1'b1), .sel(opc));  // open: out5, out22, out23, out30
endmodule

module A_register_read_enable_logic (
  input  [4:0] opc,
  output out_2
);

  wire ADD, ADDI, AND, BR, INV, JMP, JSR, LD, LDFI, LIH, LIL0, LIL1, MOV, MOVF, MSRF, MSRP, NOP, NOT, OR,
       or_1_out, ROL, ROR, RTI, SHL, SHR, ST, SUB, SWI, XOR;

  or or_1 (or_1_out, AND, JSR, SUB, ADDI, ADD, ST, LD, MOV, NOT, XOR, OR);
  or or_2 (out_2, ROR, ROL, or_1_out, SHL, SHR);
  Demultiplexer #(.select(5), .enable("false")) demultiplexer_1 (
    .out0(LD), .out1(SUB), .out2(AND), .out3(INV), .out4(ADD), .out6(NOT), .out7(NOP), .out8(BR), .out9(OR),
    .out10(LIH), .out11(LIL0), .out12(ROR), .out13(ROL), .out14(SHR), .out15(SHL), .out16(ST), .out17(XOR),
    .out18(JMP), .out19(LDFI), .out20(ADDI), .out21(LIL1), .out24(JSR), .out25(MOVF), .out26(MSRP),
    .out27(MSRF), .out28(SWI), .out29(RTI), .out31(MOV), .in(1'b1), .sel(opc));  // open: out5, out22, out23, out30
endmodule

module B_register_read_enable_logic (
  input  [4:0] opc,
  output out_2
);

  wire ADD, ADDI, AND, BR, INV, JMP, JSR, LD, LDFI, LIH, LIL0, LIL1, MOV, MOVF, MSRF, MSRP, NOP, NOT, OR,
       ROL, ROR, RTI, SHL, SHR, ST, SUB, SWI, XOR;

  or or_1 (out_2, INV, AND, JMP, SUB, ADD, ST, LD, LIL1, LIL0, LIH, XOR, OR);
  Demultiplexer #(.select(5), .enable("false")) demultiplexer_1 (
    .out0(LD), .out1(SUB), .out2(AND), .out3(INV), .out4(ADD), .out6(NOT), .out7(NOP), .out8(BR), .out9(OR),
    .out10(LIH), .out11(LIL0), .out12(ROR), .out13(ROL), .out14(SHR), .out15(SHL), .out16(ST), .out17(XOR),
    .out18(JMP), .out19(LDFI), .out20(ADDI), .out21(LIL1), .out24(JSR), .out25(MOVF), .out26(MSRP),
    .out27(MSRF), .out28(SWI), .out29(RTI), .out31(MOV), .in(1'b1), .sel(opc));  // open: out5, out22, out23, out30
endmodule

module Flags_register (
  input  [7:0] \input ,
  input  W_en,
  input  A,
  input  [2:0] R_,
  output flag_br,
  output I_flag,
  output out_7,
  output out_8,
  output out_9,
  output out_10,
  output out_11,
  output extra_flag
);

  wire and_1_out, and_2_out, and_3_out, and_4_out, and_5_out, and_6_out, and_7_out, clock_1_out,
       decoder_1_out0, decoder_1_out1, decoder_1_out2, decoder_1_out3, decoder_1_out4, decoder_1_out5,
       decoder_1_out6, decoder_1_out7;
  wire [0:0] register_1_q;

  Register register_1 (
    .D(\input ), .en(W_en), .Q({extra_flag, out_11, out_10, out_9, out_8, out_7, I_flag, register_1_q[0]}),
    .clk(clock_1_out));  // open: clr
  Clock clock_1 (.out(clock_1_out));
  Decoder #(.select(3)) decoder_1 (
    .out0(decoder_1_out0), .out1(decoder_1_out1), .out2(decoder_1_out2), .out3(decoder_1_out3),
    .out4(decoder_1_out4), .out5(decoder_1_out5), .out6(decoder_1_out6), .out7(decoder_1_out7), .sel(R_));  // open: en
  and and_1 (and_1_out, decoder_1_out5, out_10);
  and and_2 (and_2_out, decoder_1_out6, out_11);
  and and_3 (and_3_out, decoder_1_out3, out_8);
  and and_4 (and_4_out, decoder_1_out4, out_9);
  and and_5 (and_5_out, decoder_1_out2, out_7);
  and and_6 (and_6_out, decoder_1_out1, I_flag);
  and and_7 (and_7_out, A, decoder_1_out0);
  or or_1 (flag_br, and_7_out, and_6_out, and_5_out, and_3_out, and_4_out, and_1_out, and_2_out);

  // Other names for the same wires on the sheet: I = I_flag; Z = out_7; N = out_8; O = out_9; C = out_10; E = out_11;
  //   extra = extra_flag
endmodule
